// Logisim project ALU74181.circ as structural Verilog: 1 circuit, main circuit main
module main (
);

  wire and_1_out, and_2_out, and_3_out, and_4_out, and_5_out, and_6_out, and_7_out, and_8_out, and_9_out,
       and_10_out, and_11_out, and_12_out, and_13_out, and_14_out, and_15_out, and_16_out, and_17_out,
       and_18_out, and_19_out, and_20_out, button_1_out, button_2_out, button_3_out, button_4_out,
       button_5_out, button_6_out, button_7_out, button_8_out, nor_1_out, nor_2_out, nor_3_out, nor_4_out,
       nor_5_out, nor_6_out, nor_7_out, nor_8_out, not_1_out, not_2_out, not_3_out, not_4_out, undriven,
       undriven_2, undriven_3, undriven_4;

  LED led_1 ();  // open: in
  LED led_2 ();  // open: in
  LED led_3 ();  // open: in
  LED led_4 ();  // open: in
  Button button_1 (.out(button_1_out));
  Button button_2 (.out(button_2_out));
  Button button_3 (.out(button_3_out));
  Button button_4 (.out(button_4_out));
  Button button_5 (.out(button_5_out));
  Button button_6 (.out(button_6_out));
  Button button_7 (.out(button_7_out));
  Button button_8 (.out(button_8_out));
  not not_1 (not_1_out, button_1_out);
  not not_2 (not_2_out, button_3_out);
  not not_3 (not_3_out, button_5_out);
  not not_4 (not_4_out, button_7_out);
  and and_1 (and_1_out, button_1_out, undriven_4, button_2_out);
  and and_2 (and_2_out, button_2_out, undriven_3, not_1_out);
  and and_3 (and_3_out, not_1_out, undriven_2);
  and and_4 (and_4_out, undriven, button_1_out);
  buf and_5 (and_5_out, button_2_out);  // AND_Gate
  and and_6 (and_6_out, button_3_out, undriven_4, button_4_out);
  and and_7 (and_7_out, button_4_out, undriven_3, not_2_out);
  and and_8 (and_8_out, not_2_out, undriven_2);
  and and_9 (and_9_out, undriven, button_3_out);
  buf and_10 (and_10_out, button_4_out);  // AND_Gate
  and and_11 (and_11_out, button_5_out, undriven_4, button_6_out);
  and and_12 (and_12_out, button_6_out, undriven_3, not_3_out);
  and and_13 (and_13_out, not_3_out, undriven_2);
  and and_14 (and_14_out, undriven, button_5_out);
  buf and_15 (and_15_out, button_6_out);  // AND_Gate
  and and_16 (and_16_out, button_7_out, undriven_4, button_8_out);
  and and_17 (and_17_out, button_8_out, undriven_3, not_4_out);
  and and_18 (and_18_out, not_4_out, undriven_2);
  and and_19 (and_19_out, undriven, button_7_out);
  buf and_20 (and_20_out, button_8_out);  // AND_Gate
  nor nor_1 (nor_1_out, and_1_out, and_2_out);
  LED led_5 (.in(nor_1_out));
  nor nor_2 (nor_2_out, and_3_out, and_4_out, and_5_out);
  LED led_6 (.in(nor_2_out));
  LED led_7 (.in(nor_3_out));
  nor nor_3 (nor_3_out, and_6_out, and_7_out);
  nor nor_4 (nor_4_out, and_8_out, and_9_out, and_10_out);
  LED led_8 (.in(nor_4_out));
  nor nor_5 (nor_5_out, and_11_out, and_12_out);
  LED led_9 (.in(nor_5_out));
  nor nor_6 (nor_6_out, and_13_out, and_14_out, and_15_out);
  LED led_10 (.in(nor_6_out));
  LED led_11 (.in(nor_7_out));
  nor nor_7 (nor_7_out, and_16_out, and_17_out);
  LED led_12 (.in(nor_8_out));
  nor nor_8 (nor_8_out, and_18_out, and_19_out, and_20_out);

  // Notes on the sheet:
  //   S1
  //   S0
  //   S3
  //   S2
  //   B3
  //   A3
  //   B2
  //   A2
  //   B1
  //   A1
  //   B0
  //   A0
  //   why is there a random ahhh and gate here
endmodule
